// Digital circuit Processor.dig as structural Verilog
// Simple processor based on the MIPS architecture. 
// It is a Harvard single-cycle CPU.
// {{de Einfacher Prozessor, der an die MIPS-Architektur 
// angelehnt ist. Es handelt sich um eine Harvard 
// Single-Cycle CPU.}}
module Processor (
  input  Clock,
  output [15:0] A,
  output [15:0] D,
  output ioW,
  output ioR
);

  wire abs, alu2D, alu_1_carry, alu_1_neg, alu_1_zero, branch_1_jmp, flags_1_co, flags_1_no, flags_1_zo, imm,
       ld, muxA, RetI, sf, src2D, st, stPC, WE;
  wire [1:0] iem;
  wire [2:0] br, muxB;
  wire [4:0] aluOp;
  wire [15:0] imreg_1_imm, multiplexer_1_out, multiplexer_2_out, pc_1_next, pc_1_pc, register_1_rdest,
       register_1_rsrc, rom_1_d, signext_1__5d, signext_1__5s, signext_1__9sd;

  PC pc_1 (.ALU(A), .C(Clock), .abs(abs), .rel(branch_1_jmp), .Next(pc_1_next), .PC(pc_1_pc));
  ROM #(.AddrBits(16), .isProgramMemory("true"), .Bits(16)) rom_1 (.A(pc_1_pc), .sel(1'b1), .D(rom_1_d));
  assign D = stPC ? pc_1_next : 16'bz;  // Driver driver_1
  Control control_1 (
    .Op(rom_1_d[15:8]), .stPC(stPC), .WE(WE), .imm(imm), .iem(iem), .absJmp(abs), .muxB(muxB), .src2D(src2D),
    .muxA(muxA), .alu2D(alu2D), .aluOp(aluOp), .storeFlags(sf), .branch(br), .ramSt(st), .ramLd(ld),
    .ioW(ioW), .ioR(ioR), .RetI(RetI));
  Register register_1 (
    .WD(D), .C(Clock), .src(rom_1_d[3:0]), .dest(rom_1_d[7:4]), .WE(WE), .Rdest(register_1_rdest),
    .Rsrc(register_1_rsrc));
  ImReg imreg_1 (.en(imm), .iem(iem), .C(Clock), .inst(rom_1_d), .imm(imreg_1_imm));
  SignExt signext_1 (.inst(rom_1_d), ._5S(signext_1__5s), ._9SD(signext_1__9sd), ._5D(signext_1__5d));
  assign D = src2D ? register_1_rsrc : 16'bz;  // Driver driver_2
  Multiplexer #(.Bits(16)) multiplexer_1 (
    .sel(muxA), .in_0(register_1_rdest), .in_1(register_1_rsrc), .out(multiplexer_1_out));
  Multiplexer #(.Selector_Bits(3), .Bits(16)) multiplexer_2 (
    .sel(muxB), .in_0(register_1_rsrc), .in_1({16{1'b0}}), .in_2(imreg_1_imm), .in_3({16{1'b0}}),
    .in_4({16{1'b0}}), .in_5(signext_1__5s), .in_6(signext_1__9sd), .in_7(signext_1__5d),
    .out(multiplexer_2_out));
  Branch branch_1 (.Z(flags_1_zo), .N(flags_1_no), .C(flags_1_co), .ctrl(br), .jmp(branch_1_jmp));
  ALU alu_1 (
    .A(multiplexer_1_out), .B(multiplexer_2_out), .Op(aluOp), .Y(A), .Zero(alu_1_zero), .Neg(alu_1_neg),
    .Carry(alu_1_carry), .Ci(flags_1_co));
  assign D = alu2D ? A : 16'bz;  // Driver driver_3
  Flags flags_1 (
    .Zi(alu_1_zero), .Ni(alu_1_neg), .Ci(alu_1_carry), .C(Clock), .store(sf), .Zo(flags_1_zo),
    .No(flags_1_no), .Co(flags_1_co));
  RAMSinglePort #(.AddrBits(16), .Bits(16), .Addr_Bits(16)) mem (.A(A), .str(st), .C(Clock), .ld(ld), .D(D));
  Graphics graphics_1 (.A(A), .R(ioR), .C(Clock), .W(ioW), .D(D));

  // Other names for the same wires on the sheet: C = Clock

  // Notes on the sheet:
  //   Clock: Hz: 2147483647
  //   A: Address bus
  //   {{de Adressbus}}
  //   D: Data Bus
  //   {{de Datenbus}}
  //   ioW: io write enable
  //   {{de IO Schreibfreigabe}}
  //   ioR: io read enable
  //   {{de IO Lesefreigabe}}
  //   contents of rom_1 (hex, n*v repeats v):
  //   8000,961,8190,951,a90,a83,a25,a3a,10e1,afc,2bef,3d5f,c21,212f,38f9,3d20,105,116,a30,
  //   a20,aa0,8035,3ac0,4380,2180,3505,2172,3505,2173,3503,3d03,2173,3801,aa3,401a,c01,
  //   c11,c21,8014,2020,38eb,c31,8014,2030,38e6,1991,ffff,3e09,146,165,154,4400,3ddb,a70,
  //   1031,8014,f00,8060,3ab0,c21,c01,8060,3ab0,c31,8014,b00,8060,3ab0,c31,8014,b00,8060,
  //   3ab0,1021,1001,8060,3ab0,1021,1001,8060,3ab0,1031,8014,f00,8060,3ab0,1031,8014,f00,
  //   8060,3ab0,c21,c31,8015,b00,3b0c,8014,2020,3707,8014,2030,3704,4380,2180,3501,c71,
  //   3b0b,143,8014,1c40,242,246,4048,2cfe,ce1,3b0f
  //   Inputs
  //   Outputs
endmodule
